# Fritzing sketch circuit (saved by Fritzing 0.9.4)
breadboards: 1

parts:
  Part1 = Arduino Nano (Rev3.0)
  R1 = Resistor [tolerance=±5% resistance=220 package=THT]
  R3 = Resistor [tolerance=±5% resistance=220 package=THT]
  R6 = Photocell (LDR) [package=THT]
  R7 = Photocell (LDR) [package=THT]
  R8 = Photocell (LDR) [package=THT]
  R9 = Resistor [tolerance=±5% resistance=220 package=THT]
  R10 = Resistor [tolerance=±5% resistance=220 package=THT]
  R11 = Photocell (LDR) [package=THT]
  J1 = Basic Servo
  J2 = Basic Servo

nets:
  N1: Part1.D9, J2.pulse
  N2: Part1.D10, J1.pulse
  N3: Part1.A3, R1.Pin_1, R6.pin_1
  N4: Part1.A2, R3.Pin_1, R7.pin_1
  N5: Part1.A1, R8.pin_1, R9.Pin_1
  N6: Part1.A0, R10.Pin_1, R11.pin_1
  VCC: R1.Pin_0, R3.Pin_0, R9.Pin_0, R10.Pin_0, J1.vcc, J2.vcc
  GND: R6.pin_0, R7.pin_0, R8.pin_0, R11.pin_0, J1.gnd, J2.gnd
